// Logisim project 4-bit-ALU.circ as structural Verilog: 1 circuit, main circuit main
module main (
  input  Cin,
  input  [3:0] A,
  input  [2:0] in_3,
  input  [3:0] B,
  input  in_5,
  input  [2:0] comprator,
  output C4,
  output [7:0] out_8
);

  wire n7408_1_pin3, n7408_1_pin6, n7408_1_pin8, n7408_1_pin11, n7408_3_pin3, n7408_3_pin6, n7408_3_pin8,
       n7408_3_pin11, n7408_4_pin3, n7408_4_pin6, n7408_4_pin8, n7408_4_pin11, n7408_5_pin3, n7408_5_pin6,
       n7408_5_pin8, n7408_5_pin11, n74283_3_pin4, n74283_3_pin7, n74283_3_pin9, n74283_4_pin1,
       n74283_4_pin4, n74283_4_pin9, n74283_4_pin10, n74283_4_pin13, n74283_5_pin9, n74283_6_pin9,
       n74283_7_pin1, n74283_7_pin4, n74283_7_pin9, n74283_7_pin10, n74283_7_pin13;
  wire [3:0] demultiplexer_1_out0, demultiplexer_1_out1, demultiplexer_1_out2, demultiplexer_1_out3,
       demultiplexer_1_out4, demultiplexer_1_out5, demultiplexer_1_out6, demultiplexer_2_out0,
       demultiplexer_2_out1, demultiplexer_2_out2, demultiplexer_2_out3, demultiplexer_2_out4,
       demultiplexer_2_out5, demultiplexer_2_out6, not_1_out;
  wire [7:0] n74283_8_pin10, undriven, undriven_2, undriven_3, undriven_4, undriven_5, undriven_6;

  Demultiplexer #(.select(3), .width(4)) demultiplexer_1 (
    .out0(demultiplexer_1_out0), .out1(demultiplexer_1_out1), .out2(demultiplexer_1_out2),
    .out3(demultiplexer_1_out3), .out4(demultiplexer_1_out4), .out5(demultiplexer_1_out5),
    .out6(demultiplexer_1_out6), .in(A), .sel(in_3));  // open: out7
  Demultiplexer #(.select(3), .width(4)) demultiplexer_2 (
    .out0(demultiplexer_2_out0), .out1(demultiplexer_2_out1), .out2(demultiplexer_2_out2),
    .out3(demultiplexer_2_out3), .out4(demultiplexer_2_out4), .out5(demultiplexer_2_out5),
    .out6(demultiplexer_2_out6), .in(B), .sel(in_3));  // open: out7
  assign not_1_out = ~demultiplexer_2_out1;  // NOT_Gate not_1, 4 bits wide
  _74283 u_74283_1 (
    .pin1(undriven[5]), .pin2(demultiplexer_2_out0[1]), .pin3(demultiplexer_1_out0[1]), .pin4(undriven[4]),
    .pin5(demultiplexer_1_out0[0]), .pin6(demultiplexer_2_out0[0]), .pin7(Cin),
    .pin15(demultiplexer_2_out0[2]), .pin14(demultiplexer_1_out0[2]), .pin13(undriven[6]),
    .pin12(demultiplexer_1_out0[3]), .pin11(demultiplexer_2_out0[3]), .pin10(undriven[7]), .pin9(C4));
  _74283 u_74283_2 (
    .pin1(undriven_2[5]), .pin2(not_1_out[1]), .pin3(demultiplexer_1_out1[1]), .pin4(undriven_2[4]),
    .pin5(demultiplexer_1_out1[0]), .pin6(not_1_out[0]), .pin7(in_5), .pin15(not_1_out[2]),
    .pin14(demultiplexer_1_out1[2]), .pin13(undriven_2[6]), .pin12(demultiplexer_1_out1[3]),
    .pin11(not_1_out[3]), .pin10(undriven_2[7]));  // open: pin9
  _7408 u_7408_1 (
    .pin1(demultiplexer_1_out6[3]), .pin2(demultiplexer_2_out6[0]), .pin3(n7408_1_pin3),
    .pin4(demultiplexer_1_out6[3]), .pin5(demultiplexer_2_out6[1]), .pin6(n7408_1_pin6),
    .pin13(demultiplexer_2_out6[3]), .pin12(demultiplexer_1_out6[3]), .pin11(n7408_1_pin11),
    .pin10(demultiplexer_2_out6[2]), .pin9(demultiplexer_1_out6[3]), .pin8(n7408_1_pin8));
  _7408 u_7408_2 (
    .pin1(demultiplexer_1_out2[0]), .pin2(demultiplexer_2_out2[0]), .pin3(undriven_3[4]),
    .pin4(demultiplexer_1_out2[1]), .pin5(demultiplexer_2_out2[1]), .pin6(undriven_3[5]),
    .pin13(demultiplexer_2_out2[3]), .pin12(demultiplexer_1_out2[3]), .pin11(undriven_3[7]),
    .pin10(demultiplexer_2_out2[2]), .pin9(demultiplexer_1_out2[2]), .pin8(undriven_3[6]));
  _7432 u_7432_1 (
    .pin1(demultiplexer_1_out3[0]), .pin2(demultiplexer_2_out3[0]), .pin3(undriven_4[4]),
    .pin4(demultiplexer_1_out3[1]), .pin5(demultiplexer_2_out3[1]), .pin6(undriven_4[5]),
    .pin13(demultiplexer_2_out3[3]), .pin12(demultiplexer_1_out3[3]), .pin11(undriven_4[7]),
    .pin10(demultiplexer_2_out3[2]), .pin9(demultiplexer_1_out3[2]), .pin8(undriven_4[6]));
  _7486 u_7486_1 (
    .pin1(demultiplexer_1_out4[0]), .pin2(demultiplexer_2_out4[0]), .pin3(undriven_5[4]),
    .pin4(demultiplexer_1_out4[1]), .pin5(demultiplexer_2_out4[1]), .pin6(undriven_5[5]),
    .pin13(demultiplexer_2_out4[3]), .pin12(demultiplexer_1_out4[3]), .pin11(undriven_5[7]),
    .pin10(demultiplexer_2_out4[2]), .pin9(demultiplexer_1_out4[2]), .pin8(undriven_5[6]));
  _7485 u_7485_1 (
    .pin1(demultiplexer_2_out5[3]), .pin2(comprator[0]), .pin3(comprator[1]), .pin4(comprator[2]),
    .pin5(undriven_6[5]), .pin6(undriven_6[7]), .pin7(undriven_6[6]), .pin15(demultiplexer_1_out5[3]),
    .pin14(demultiplexer_2_out5[2]), .pin13(demultiplexer_1_out5[2]), .pin12(demultiplexer_1_out5[1]),
    .pin11(demultiplexer_2_out5[1]), .pin10(demultiplexer_1_out5[0]), .pin9(demultiplexer_2_out5[0]));
  _7408 u_7408_3 (
    .pin1(demultiplexer_1_out6[0]), .pin2(demultiplexer_2_out6[0]), .pin3(n7408_3_pin3),
    .pin4(demultiplexer_1_out6[0]), .pin5(demultiplexer_2_out6[1]), .pin6(n7408_3_pin6),
    .pin13(demultiplexer_2_out6[3]), .pin12(demultiplexer_1_out6[0]), .pin11(n7408_3_pin11),
    .pin10(demultiplexer_2_out6[2]), .pin9(demultiplexer_1_out6[0]), .pin8(n7408_3_pin8));
  _7408 u_7408_4 (
    .pin1(demultiplexer_1_out6[1]), .pin2(demultiplexer_2_out6[0]), .pin3(n7408_4_pin3),
    .pin4(demultiplexer_1_out6[1]), .pin5(demultiplexer_2_out6[1]), .pin6(n7408_4_pin6),
    .pin13(demultiplexer_2_out6[3]), .pin12(demultiplexer_1_out6[1]), .pin11(n7408_4_pin11),
    .pin10(demultiplexer_2_out6[2]), .pin9(demultiplexer_1_out6[1]), .pin8(n7408_4_pin8));
  _7408 u_7408_5 (
    .pin1(demultiplexer_1_out6[2]), .pin2(demultiplexer_2_out6[0]), .pin3(n7408_5_pin3),
    .pin4(demultiplexer_1_out6[2]), .pin5(demultiplexer_2_out6[1]), .pin6(n7408_5_pin6),
    .pin13(demultiplexer_2_out6[3]), .pin12(demultiplexer_1_out6[2]), .pin11(n7408_5_pin11),
    .pin10(demultiplexer_2_out6[2]), .pin9(demultiplexer_1_out6[2]), .pin8(n7408_5_pin8));
  _74283 u_74283_3 (
    .pin4(n74283_3_pin4), .pin5(n7408_4_pin11), .pin6(n7408_5_pin8), .pin7(n74283_3_pin7),
    .pin9(n74283_3_pin9));  // open: pin1, pin2, pin3, pin15, pin14, pin13, pin12, pin11, pin10
  _74283 u_74283_4 (
    .pin1(n74283_4_pin1), .pin2(n7408_4_pin3), .pin3(n7408_3_pin6), .pin4(n74283_4_pin4),
    .pin5(n7408_3_pin3), .pin15(n7408_4_pin6), .pin14(n7408_3_pin8), .pin13(n74283_4_pin13),
    .pin12(n7408_3_pin11), .pin11(n7408_4_pin8), .pin10(n74283_4_pin10), .pin9(n74283_4_pin9));  // open: pin6, pin7
  _74283 u_74283_5 (
    .pin4(n74283_8_pin10[5]), .pin5(n74283_3_pin4), .pin6(n7408_1_pin6), .pin7(n74283_3_pin9),
    .pin9(n74283_5_pin9));  // open: pin1, pin2, pin3, pin15, pin14, pin13, pin12, pin11, pin10
  _74283 u_74283_6 (
    .pin4(n74283_8_pin10[4]), .pin5(n7408_5_pin11), .pin6(n7408_1_pin8), .pin7(n74283_5_pin9),
    .pin9(n74283_6_pin9));  // open: pin1, pin2, pin3, pin15, pin14, pin13, pin12, pin11, pin10
  _74283 u_74283_7 (
    .pin1(n74283_7_pin1), .pin3(n74283_4_pin1), .pin4(n74283_7_pin4), .pin5(n74283_4_pin4),
    .pin7(n74283_4_pin9), .pin15(n7408_5_pin3), .pin14(n74283_4_pin13), .pin13(n74283_7_pin13),
    .pin12(n74283_4_pin10), .pin11(n7408_5_pin6), .pin10(n74283_7_pin10), .pin9(n74283_7_pin9));  // open: pin2, pin6
  _74283 u_74283_8 (
    .pin1(n74283_8_pin10[2]), .pin3(n74283_7_pin1), .pin4(n74283_8_pin10[3]), .pin5(n74283_7_pin4),
    .pin7(n74283_7_pin9), .pin14(n74283_7_pin13), .pin13(n74283_8_pin10[1]), .pin12(n74283_7_pin10),
    .pin11(n7408_1_pin3), .pin10(n74283_8_pin10[0]), .pin9(n74283_3_pin7));  // open: pin2, pin6, pin15
  _74283 u_74283_9 (
    .pin4(n74283_8_pin10[6]), .pin5(n7408_1_pin11), .pin7(n74283_6_pin9), .pin9(n74283_8_pin10[7]));  // open: pin1, pin2, pin3, pin6, pin15, pin14, pin13, pin12, pin11, pin10
  Multiplexer #(.select(3), .width(8)) multiplexer_1 (
    .in0(undriven), .in1(undriven_2), .in2(undriven_3), .in3(undriven_4), .in4(undriven_5), .in5(undriven_6),
    .in6(n74283_8_pin10), .out(out_8), .sel(in_3));  // open: in7
endmodule
